# Fritzing sketch star_tracker_wiring (saved by Fritzing 1.0.8)

parts:
  U1 = Star tracker controller (Rev C)
  BT2 = Battery 12 V LiFePO4
  F3 = Inline fuse holder, 3 A
  M4 = Stepper, NEMA 17 pancake
  U5 = AS5600 breakout
  U6 = GPS, GY-NEO6MV2
  CAM7 = GoPro HERO6

nets:
  N1: U1.J1.1_+12V, F3.out
  N2: U1.J1.2_GND, BT2.-
  N3: U1.J7.1_GND, U5.GND
  N4: U1.J7.2_3V3, U5.VCC
  N5: U1.J7.3_SDA, U5.SDA
  N6: U1.J7.4_SCL, U5.SCL
  N7: U1.J7.5_DIR, U5.DIR
  N8: U1.J9.1_PPS, U6.PPS
  N9: U1.J9.2_VCC, U6.VCC
  N10: U1.J9.3_RXD, U6.RX
  N11: U1.J9.4_TXD, U6.TX
  N12: U1.J9.5_GND, U6.GND
  N13: U1.J4.1_A1, M4.A1
  N14: U1.J4.2_A2, M4.A2
  N15: U1.J4.3_B1, M4.B1
  N16: U1.J4.4_B2, M4.B2
  N17: U1.J2_USB-A, CAM7.USB-C
  N18: BT2.+, F3.in

custom parts:
  Star tracker controller (Rev C): star_tracker_ctrl, 150 x 100 mm, drawn from the KiCad layout. Modules shown fitted.
  Battery 12 V LiFePO4: LiFePO4 12.8 V nominal, 14.6 V full
  Inline fuse holder, 3 A: blade or 5x20 inline holder, 3 A
  Stepper, NEMA 17 pancake: bipolar, 0.7 A. Lead colours vary: find the pairs with a meter.
  AS5600 breakout: generic 7-pin AS5600 magnetic encoder board; on the bracket
  GPS, GY-NEO6MV2: u-blox NEO-6M. PPS is not on the header: tap it at the PPS LED.
  GoPro HERO6: controlled over WiFi gpControl; powered from J2
